# Fritzing sketch distance_sensor (saved by Fritzing 0.9.3b)
breadboards: 1

parts:
  Raspberry_Pi_1 = Raspberry Pi 3 [part_number=RPI-3-V1.2]
  IC1 = MCP3008 8-channel 10-bit ADC [part_number=MCP3008]
  J2 = Infrared Proximity Sensor

nets:
  N1: Raspberry_Pi_1.GIPO10, IC1.no_name_yet#11
  N2: Raspberry_Pi_1.GIPO9, IC1.no_name_yet#12
  N3: Raspberry_Pi_1.GIPO11, IC1.no_name_yet#13
  N4: Raspberry_Pi_1.GIPO8, IC1.no_name_yet#10
  GND: Raspberry_Pi_1.GND, IC1.no_name_yet#9, IC1.no_name_yet#14, J2.GND
  5V: Raspberry_Pi_1.5V, IC1.no_name_yet#15, IC1.no_name_yet#16, J2.Vcc
  N5: IC1.no_name_yet#1, J2.Vout

notes:
  画像と実物のコードの色は異なります
  ピン - 画像 - 実物
  1(Vo) - 黄色 - 白色
  2(GRD) - 黒色 - 黄色
  3(Vcc) - 赤色 - 黒色
