# Fritzing sketch buzzer (saved by Fritzing 0.9.3b)
breadboards: 1

parts:
  J1 = Piezo Speaker
  Raspberry_Pi_1 = Raspberry Pi 3 [part_number=RPI-3-V1.2]

nets:
  N1: J1.pin1, Raspberry_Pi_1.GND
  N2: J1.pin2, Raspberry_Pi_1.GPIO19
