# Fritzing sketch input_switch (saved by Fritzing 0.9.3b)
breadboards: 1

parts:
  Raspberry_Pi_1 = Raspberry Pi 3 [part_number=RPI-3-V1.2]
  S6 = Pushbutton [package="[SMD]"]
  LED1 = smd LED [color="Red (633nm)" package="0603 [SMD]"]
  R1 = Resistor [tolerance=±5% resistance=470 package=THT]
  R2 = Resistor [tolerance=±5% resistance=470 package=THT]

nets:
  N1: Raspberry_Pi_1.GPIO21, S6.Pin_3, S6.Pin_4, R2.Pin_1
  N2: Raspberry_Pi_1.GPIO18, LED1.anode
  N3: Raspberry_Pi_1.GND, S6.Pin_1, S6.Pin_2, R1.Pin_0
  N4: Raspberry_Pi_1.5V, R2.Pin_0
  N5: LED1.cathode, R1.Pin_1
