# Fritzing sketch new_motor_forward_and_back (saved by Fritzing 0.9.4)
breadboards: 1

parts:
  M1 = DC Motor
  Raspberry_Pi_1 = Raspberry Pi 3 [part_number=RPI-3-V1.2]
  U1 = SIP - 8 pins [chip_label=IC package="SIP (Single Inline) [THT]"]

nets:
  N1: M1.pin_1, U1.pin6
  N2: M1.pin_2, U1.pin8
  N3: Raspberry_Pi_1.GPIO21, U1.pin2
  N4: Raspberry_Pi_1.GPIO20, U1.pin3
  N5: Raspberry_Pi_1.GPIO18, U1.pin4
  N6: Raspberry_Pi_1.GND, U1.pin1, U1.pin7
  N7: Raspberry_Pi_1.5V, U1.pin5

custom parts:
  SIP - 8 pins: A SIP stand-in part for whatever you want. With 8 pins on a 300 mil single inline package (SIP) footprint.
