# Fritzing sketch input_switch (saved by Fritzing 0.9.3b)
breadboards: 1

parts:
  Raspberry_Pi_1 = Raspberry Pi 3 [part_number=RPI-3-V1.2]
  S6 = Pushbutton [package="[SMD]"]
  LED1 = smd LED [color="Red (633nm)" package="0603 [SMD]"]
  R1 = Resistor [tolerance=±5% resistance=1k package=THT]

nets:
  N1: Raspberry_Pi_1.GPIO23, LED1.cathode, R1.Pin_0
  N2: Raspberry_Pi_1.GND, R1.Pin_1
  N3: Raspberry_Pi_1.5V, S6.Pin_1, S6.Pin_2
  N4: S6.Pin_3, S6.Pin_4, LED1.anode
