# Fritzing sketch l_chika (saved by Fritzing 0.9.3b)
breadboards: 1

parts:
  Raspberry_Pi_1 = Raspberry Pi 3 [part_number=RPI-3-V1.2]
  LED1 = LED - 5mm [color="Red (633nm)" package="5 mm [THT]"]
  R1 = Resistor [tolerance=±5% resistance=10k package=THT]

nets (from the schematic view):
  N1: Raspberry_Pi_1.GPIO21, LED1.anode, R1.Pin_1
  N2: LED1.cathode, R1.Pin_0
