# Fritzing sketch motor_forward_and_back (saved by Fritzing 0.9.3b)
breadboards: 1

parts:
  U1 = TA7291P [package=HSIP10-P-2.54(THT)]
  Raspberry_Pi_2 = Raspberry Pi 3 [part_number=RPI-3-V1.2]
  M1 = DC Motor

nets:
  GND: U1.GND, Raspberry_Pi_2.GND
  N1: U1.OUT1, M1.pin_1
  N2: U1.Vref, Raspberry_Pi_2.GPIO18
  N3: U1.IN1, Raspberry_Pi_2.GPIO20
  N4: U1.IN2, Raspberry_Pi_2.GPIO21
  VCC: U1.Vcc, U1.Vs, Raspberry_Pi_2.5V
  N5: U1.OUT2, M1.pin_2

custom parts:
  TA7291P: The IC are Full-Bridge Driver. 4 modes available (CW / CCW / STOP / BRAKE) and PWM control. Output current:1.0 A (AVE.) 2.0 A (PEAK)
