# Fritzing sketch panzer_vor_2 (saved by Fritzing 0.9.3b)
breadboards: 1

parts:
  Raspberry_Pi_1 = Raspberry Pi 3 [part_number=RPI-3-V1.2]
  M2 = DC Motor
  M3 = DC Motor

nets:
  N1: Raspberry_Pi_1.GND, M2.pin_1, M3.pin_1

notes:
  ピンク色がモータードライバー
  1番PinはGRD
